// Logisim project uni02_q_clc.circ as structural Verilog: 1 circuit, main circuit main
module main (
);

  wire Licznik_bit0_q, Licznik_bit1_q, nor_1_out, nor_2_out, nor_3_out, nor_4_out, nor_5_out, or_1_out,
       Out_q, \Resetujący_q , Sys_clk_out, Tacho_out;

  Clock #(.highDuration(41), .lowDuration(41)) Tacho (.out(Tacho_out));
  Clock #(.highDuration(40), .lowDuration(40)) Sys_clk (.out(Sys_clk_out));
  or or_1 (or_1_out, ~Licznik_bit1_q, ~Licznik_bit0_q);  // OR_Gate
  J_K_Flip_Flop Licznik_bit0 (
    .J(or_1_out), .clk(Tacho_out), .K(or_1_out), .Q(Licznik_bit0_q), .reset(\Resetujący_q ));  // open: Qn, preset, en
  nor nor_1 (nor_1_out, Licznik_bit1_q, ~Licznik_bit0_q);  // NOR_Gate
  D_Flip_Flop \Resetujący  (
    .clk(nor_2_out), .D(1'b1), .Q(\Resetujący_q ), .reset(\Resetujący_q ));  // open: Qn, preset, en
  nor nor_2 (nor_2_out, Sys_clk_out, Sys_clk_out);
  J_K_Flip_Flop Licznik_bit1 (
    .J(nor_1_out), .clk(Tacho_out), .K(nor_1_out), .Q(Licznik_bit1_q), .reset(\Resetujący_q ));  // open: Qn, preset, en
  nor nor_3 (nor_3_out, ~Licznik_bit1_q, ~Licznik_bit0_q);  // NOR_Gate
  nor nor_4 (nor_4_out, ~Licznik_bit1_q, ~Licznik_bit0_q, ~Sys_clk_out);  // NOR_Gate
  nor nor_5 (nor_5_out, Licznik_bit0_q, Licznik_bit1_q, ~\Resetujący_q );  // NOR_Gate
  D_Flip_Flop Out (.clk(nor_4_out), .D(nor_3_out), .Q(Out_q), .reset(nor_5_out));  // open: Qn, preset, en
endmodule
